// Logisim project control-logic.circ as structural Verilog: 1 circuit, main circuit control_logic
module control_logic (
  input  [31:0] Instruction,
  input  BrEq,
  input  BrLt,
  output PCSel,
  output RegWEn,
  output [2:0] ImmSel,
  output BrUn,
  output ASel,
  output BSel,
  output [3:0] ALUSel,
  output MemWEn,
  output [1:0] WBSel
);

  wire and_1_out, and_2_out, and_3_out, and_4_out, comparator_2_eq, comparator_3_eq, comparator_4_eq,
       comparator_5_eq, comparator_6_eq, comparator_7_eq, comparator_8_eq, comparator_9_eq, comparator_10_eq,
       comparator_11_eq, comparator_12_eq, comparator_14_eq, comparator_15_eq, comparator_16_eq,
       comparator_17_eq, comparator_18_eq, comparator_19_eq, comparator_20_eq, comparator_21_eq,
       comparator_22_eq, comparator_23_eq, comparator_24_eq, comparator_25_eq, comparator_26_eq,
       comparator_27_eq, comparator_28_eq, comparator_29_eq, comparator_30_eq, comparator_31_eq,
       comparator_32_eq, comparator_33_eq, comparator_34_eq, comparator_35_eq, comparator_36_eq,
       comparator_37_eq, comparator_41_eq, comparator_42_eq, comparator_43_eq, comparator_44_eq,
       comparator_45_eq, comparator_46_eq, comparator_47_eq, comparator_48_eq, comparator_49_eq,
       comparator_50_eq, comparator_51_eq, comparator_52_eq, comparator_53_eq, comparator_57_eq, is_add,
       is_addi, is_and, is_andi, is_auipc, is_B, is_beq, is_bge, is_bgeu, is_blt, is_bltu, is_bne, is_I,
       is_jal, is_jalr, is_lb, is_lh, is_load, is_lui, is_lw, is_mul, is_mulh, is_mulhu, is_or, is_ori, is_R,
       is_s, is_sb, is_sh, is_sll, is_slli, is_slt, is_slti, is_sra, is_srai, is_srl, is_srli, is_sub, is_sw,
       is_xor, is_xori, not_1_out, not_2_out, or_1_out, or_2_out, or_3_out;
  wire [5:0] priority_encoder_1_p25;
  wire [15:14] rom_1_data;

  ROM #(.addrWidth(6), .dataWidth(16)) rom_1 (
    .addr(priority_encoder_1_p25),
    .data({rom_1_data, WBSel, MemWEn, ALUSel, BSel, ASel, BrUn, ImmSel, RegWEn}));
  // Priority_Encoder #(.select_enc(6)) priority_encoder_1: pin names not known; wires that end beside it: is_xor, is_srl, is_sra, is_or, is_and, is_lb, is_lh, is_lw, is_addi, is_slli, is_slti, is_xori, is_srli, is_srai, is_ori, is_andi, is_sb, is_sh, is_sw, is_beq, is_bne, is_blt, is_bge, is_bltu, priority_encoder_1_p25, is_bgeu, is_auipc, is_lui, is_jal, is_jalr
  not not_1 (not_1_out, BrEq);
  not not_2 (not_2_out, BrLt);
  and and_1 (and_1_out, is_bne, not_1_out);
  or or_1 (or_1_out, is_jalr, is_jal);
  and and_2 (and_2_out, is_beq, BrEq);
  or or_2 (or_2_out, is_bltu, is_blt);
  or or_3 (or_3_out, is_bgeu, is_bge);
  and and_3 (and_3_out, or_2_out, BrLt);
  and and_4 (and_4_out, or_3_out, not_2_out);
  Comparator #(.mode("unsigned"), .width(7)) comparator_1 (
    .a(Instruction[6:0]), .b(7'b0010011), .eq(is_I));  // open: gt, lt
  or or_4 (PCSel, or_1_out, and_2_out, and_3_out, and_4_out, and_1_out);
  Comparator #(.mode("unsigned"), .width(3)) comparator_2 (
    .a(Instruction[14:12]), .b(3'b000), .eq(comparator_2_eq));  // open: gt, lt
  Comparator #(.mode("unsigned"), .width(3)) comparator_3 (
    .a(Instruction[14:12]), .b(3'b111), .eq(comparator_3_eq));  // open: gt, lt
  Comparator #(.mode("unsigned"), .width(3)) comparator_4 (
    .a(Instruction[14:12]), .b(3'b110), .eq(comparator_4_eq));  // open: gt, lt
  Comparator #(.mode("unsigned"), .width(3)) comparator_5 (
    .a(Instruction[14:12]), .b(3'b100), .eq(comparator_5_eq));  // open: gt, lt
  Comparator #(.mode("unsigned"), .width(3)) comparator_6 (
    .a(Instruction[14:12]), .b(3'b010), .eq(comparator_6_eq));  // open: gt, lt
  Comparator #(.mode("unsigned"), .width(7)) comparator_7 (
    .a(Instruction[31:25]), .b({7{1'b0}}), .eq(comparator_7_eq));  // open: gt, lt
  Comparator #(.mode("unsigned"), .width(3)) comparator_8 (
    .a(Instruction[14:12]), .b(3'b101), .eq(comparator_8_eq));  // open: gt, lt
  Comparator #(.mode("unsigned"), .width(7)) comparator_9 (
    .a(Instruction[31:25]), .b(7'b0100000), .eq(comparator_9_eq));  // open: gt, lt
  Comparator #(.mode("unsigned"), .width(3)) comparator_10 (
    .a(Instruction[14:12]), .b(3'b101), .eq(comparator_10_eq));  // open: gt, lt
  Comparator #(.mode("unsigned"), .width(7)) comparator_11 (
    .a(Instruction[31:25]), .b({7{1'b0}}), .eq(comparator_11_eq));  // open: gt, lt
  Comparator #(.mode("unsigned"), .width(3)) comparator_12 (
    .a(Instruction[14:12]), .b(3'b001), .eq(comparator_12_eq));  // open: gt, lt
  and and_5 (is_addi, comparator_2_eq, is_I);
  and and_6 (is_andi, comparator_3_eq, is_I);
  and and_7 (is_ori, comparator_4_eq, is_I);
  and and_8 (is_xori, comparator_5_eq, is_I);
  and and_9 (is_slti, comparator_6_eq, is_I);
  and and_10 (is_srli, is_I, comparator_7_eq, comparator_8_eq);
  and and_11 (is_srai, is_I, comparator_9_eq, comparator_10_eq);
  and and_12 (is_slli, is_I, comparator_11_eq, comparator_12_eq);
  Comparator #(.mode("unsigned"), .width(7)) comparator_13 (
    .a(Instruction[6:0]), .b(7'b0110011), .eq(is_R));  // open: gt, lt
  Comparator #(.mode("unsigned"), .width(7)) comparator_14 (
    .a(Instruction[31:25]), .b({7{1'b0}}), .eq(comparator_14_eq));  // open: gt, lt
  Comparator #(.mode("unsigned"), .width(3)) comparator_15 (
    .a(Instruction[14:12]), .b(3'b000), .eq(comparator_15_eq));  // open: gt, lt
  Comparator #(.mode("unsigned"), .width(7)) comparator_16 (
    .a(Instruction[31:25]), .b(7'b0100000), .eq(comparator_16_eq));  // open: gt, lt
  Comparator #(.mode("unsigned"), .width(3)) comparator_17 (
    .a(Instruction[14:12]), .b(3'b000), .eq(comparator_17_eq));  // open: gt, lt
  Comparator #(.mode("unsigned"), .width(7)) comparator_18 (
    .a(Instruction[31:25]), .b({7{1'b0}}), .eq(comparator_18_eq));  // open: gt, lt
  Comparator #(.mode("unsigned"), .width(3)) comparator_19 (
    .a(Instruction[14:12]), .b(3'b111), .eq(comparator_19_eq));  // open: gt, lt
  Comparator #(.mode("unsigned"), .width(7)) comparator_20 (
    .a(Instruction[31:25]), .b({7{1'b0}}), .eq(comparator_20_eq));  // open: gt, lt
  Comparator #(.mode("unsigned"), .width(3)) comparator_21 (
    .a(Instruction[14:12]), .b(3'b110), .eq(comparator_21_eq));  // open: gt, lt
  Comparator #(.mode("unsigned"), .width(7)) comparator_22 (
    .a(Instruction[31:25]), .b({7{1'b0}}), .eq(comparator_22_eq));  // open: gt, lt
  Comparator #(.mode("unsigned"), .width(3)) comparator_23 (
    .a(Instruction[14:12]), .b(3'b100), .eq(comparator_23_eq));  // open: gt, lt
  Comparator #(.mode("unsigned"), .width(7)) comparator_24 (
    .a(Instruction[31:25]), .b({7{1'b0}}), .eq(comparator_24_eq));  // open: gt, lt
  Comparator #(.mode("unsigned"), .width(3)) comparator_25 (
    .a(Instruction[14:12]), .b(3'b001), .eq(comparator_25_eq));  // open: gt, lt
  Comparator #(.mode("unsigned"), .width(7)) comparator_26 (
    .a(Instruction[31:25]), .b({7{1'b0}}), .eq(comparator_26_eq));  // open: gt, lt
  Comparator #(.mode("unsigned"), .width(3)) comparator_27 (
    .a(Instruction[14:12]), .b(3'b101), .eq(comparator_27_eq));  // open: gt, lt
  Comparator #(.mode("unsigned"), .width(7)) comparator_28 (
    .a(Instruction[31:25]), .b(7'b0100000), .eq(comparator_28_eq));  // open: gt, lt
  Comparator #(.mode("unsigned"), .width(3)) comparator_29 (
    .a(Instruction[14:12]), .b(3'b101), .eq(comparator_29_eq));  // open: gt, lt
  Comparator #(.mode("unsigned"), .width(7)) comparator_30 (
    .a(Instruction[31:25]), .b({7{1'b0}}), .eq(comparator_30_eq));  // open: gt, lt
  Comparator #(.mode("unsigned"), .width(3)) comparator_31 (
    .a(Instruction[14:12]), .b(3'b010), .eq(comparator_31_eq));  // open: gt, lt
  Comparator #(.mode("unsigned"), .width(7)) comparator_32 (
    .a(Instruction[31:25]), .b(7'b0000001), .eq(comparator_32_eq));  // open: gt, lt
  Comparator #(.mode("unsigned"), .width(3)) comparator_33 (
    .a(Instruction[14:12]), .b(3'b000), .eq(comparator_33_eq));  // open: gt, lt
  Comparator #(.mode("unsigned"), .width(7)) comparator_34 (
    .a(Instruction[31:25]), .b(7'b0000001), .eq(comparator_34_eq));  // open: gt, lt
  Comparator #(.mode("unsigned"), .width(3)) comparator_35 (
    .a(Instruction[14:12]), .b(3'b001), .eq(comparator_35_eq));  // open: gt, lt
  Comparator #(.mode("unsigned"), .width(7)) comparator_36 (
    .a(Instruction[31:25]), .b(7'b0000001), .eq(comparator_36_eq));  // open: gt, lt
  Comparator #(.mode("unsigned"), .width(3)) comparator_37 (
    .a(Instruction[14:12]), .b(3'b011), .eq(comparator_37_eq));  // open: gt, lt
  and and_13 (is_add, is_R, comparator_14_eq, comparator_15_eq);
  and and_14 (is_sub, is_R, comparator_16_eq, comparator_17_eq);
  and and_15 (is_and, is_R, comparator_18_eq, comparator_19_eq);
  and and_16 (is_or, is_R, comparator_20_eq, comparator_21_eq);
  and and_17 (is_xor, is_R, comparator_22_eq, comparator_23_eq);
  and and_18 (is_sll, is_R, comparator_24_eq, comparator_25_eq);
  and and_19 (is_srl, is_R, comparator_26_eq, comparator_27_eq);
  and and_20 (is_sra, is_R, comparator_28_eq, comparator_29_eq);
  and and_21 (is_slt, is_R, comparator_30_eq, comparator_31_eq);
  and and_22 (is_mul, is_R, comparator_32_eq, comparator_33_eq);
  and and_23 (is_mulh, is_R, comparator_34_eq, comparator_35_eq);
  and and_24 (is_mulhu, is_R, comparator_36_eq, comparator_37_eq);
  Comparator #(.mode("unsigned"), .width(7)) comparator_38 (
    .a(Instruction[6:0]), .b(7'b1100011), .eq(is_B));  // open: gt, lt
  Comparator #(.mode("unsigned"), .width(7)) comparator_39 (
    .a(Instruction[6:0]), .b(7'b0000011), .eq(is_load));  // open: gt, lt
  Comparator #(.mode("unsigned"), .width(7)) comparator_40 (
    .a(Instruction[6:0]), .b(7'b0100011), .eq(is_s));  // open: gt, lt
  Comparator #(.mode("unsigned"), .width(3)) comparator_41 (
    .a(Instruction[14:12]), .b(3'b000), .eq(comparator_41_eq));  // open: gt, lt
  Comparator #(.mode("unsigned"), .width(3)) comparator_42 (
    .a(Instruction[14:12]), .b(3'b101), .eq(comparator_42_eq));  // open: gt, lt
  Comparator #(.mode("unsigned"), .width(3)) comparator_43 (
    .a(Instruction[14:12]), .b(3'b111), .eq(comparator_43_eq));  // open: gt, lt
  Comparator #(.mode("unsigned"), .width(3)) comparator_44 (
    .a(Instruction[14:12]), .b(3'b100), .eq(comparator_44_eq));  // open: gt, lt
  Comparator #(.mode("unsigned"), .width(3)) comparator_45 (
    .a(Instruction[14:12]), .b(3'b110), .eq(comparator_45_eq));  // open: gt, lt
  Comparator #(.mode("unsigned"), .width(3)) comparator_46 (
    .a(Instruction[14:12]), .b(3'b001), .eq(comparator_46_eq));  // open: gt, lt
  Comparator #(.mode("unsigned"), .width(3)) comparator_47 (
    .a(Instruction[14:12]), .b(3'b000), .eq(comparator_47_eq));  // open: gt, lt
  Comparator #(.mode("unsigned"), .width(3)) comparator_48 (
    .a(Instruction[14:12]), .b(3'b001), .eq(comparator_48_eq));  // open: gt, lt
  Comparator #(.mode("unsigned"), .width(3)) comparator_49 (
    .a(Instruction[14:12]), .b(3'b010), .eq(comparator_49_eq));  // open: gt, lt
  Comparator #(.mode("unsigned"), .width(3)) comparator_50 (
    .a(Instruction[14:12]), .b(3'b000), .eq(comparator_50_eq));  // open: gt, lt
  Comparator #(.mode("unsigned"), .width(3)) comparator_51 (
    .a(Instruction[14:12]), .b(3'b001), .eq(comparator_51_eq));  // open: gt, lt
  Comparator #(.mode("unsigned"), .width(3)) comparator_52 (
    .a(Instruction[14:12]), .b(3'b010), .eq(comparator_52_eq));  // open: gt, lt
  and and_25 (is_beq, comparator_41_eq, is_B);
  and and_26 (is_bge, comparator_42_eq, is_B);
  and and_27 (is_bgeu, comparator_43_eq, is_B);
  and and_28 (is_blt, comparator_44_eq, is_B);
  and and_29 (is_bltu, comparator_45_eq, is_B);
  and and_30 (is_bne, comparator_46_eq, is_B);
  and and_31 (is_lb, comparator_47_eq, is_load);
  and and_32 (is_lh, comparator_48_eq, is_load);
  and and_33 (is_lw, comparator_49_eq, is_load);
  and and_34 (is_sb, comparator_50_eq, is_s);
  and and_35 (is_sh, comparator_51_eq, is_s);
  and and_36 (is_sw, comparator_52_eq, is_s);
  Comparator #(.mode("unsigned"), .width(7)) comparator_53 (
    .a(Instruction[6:0]), .b(7'b1100111), .eq(comparator_53_eq));  // open: gt, lt
  Comparator #(.mode("unsigned"), .width(7)) comparator_54 (
    .a(Instruction[6:0]), .b(7'b1101111), .eq(is_jal));  // open: gt, lt
  Comparator #(.mode("unsigned"), .width(7)) comparator_55 (
    .a(Instruction[6:0]), .b(7'b0010111), .eq(is_auipc));  // open: gt, lt
  Comparator #(.mode("unsigned"), .width(7)) comparator_56 (
    .a(Instruction[6:0]), .b(7'b0110111), .eq(is_lui));  // open: gt, lt
  Comparator #(.mode("unsigned"), .width(3)) comparator_57 (
    .a(Instruction[14:12]), .b(3'b000), .eq(comparator_57_eq));  // open: gt, lt
  and and_37 (is_jalr, comparator_57_eq, comparator_53_eq);

  // Other names for the same wires on the sheet: opcode[6:0] = Instruction[6:0]; fun3[2:0] = Instruction[14:12];
  //   fun7[6:0] = Instruction[31:25]

  // Notes on the sheet:
  //   INPUTS to your circuit
  //   Connect ROM Input here ->
  //   contents of rom_1 (hex, n*v repeats v):
  //   1061 1461 1661 10e1 14e1 15e1 1161 1261 12e1 16e1 1361 13e1 21 21 21 1021 10a1 1121 1221 12a1 16a1
  //   1321 13a1 822 822 822 4*4 14 14 1007 1787 2009 2021
  //   ROM FOR CONTROL LOGIC
  //   DON'T CHANGE THE LOCATIONS OF THE INPUTS AND OUTPUTS!
  //   This is only if you choose to do the ROM option
  //   CONNECT
  //   WIRE
  //   TO
  //   USE
  //   ROM
  //   OUTPUT from your circuit
  //   Reminder: If using ROM, use combinational logic for PCSel
endmodule
