// Logisim project cpu.circ as structural Verilog: 1 circuit, main circuit cpu
module cpu (
  input  clk,
  input  [31:0] Instruction,
  input  [31:0] MemReadData,
  output [31:0] MemAddress,
  output [31:0] ProgramCounter,
  output [31:0] ra,
  output [31:0] sp,
  output [31:0] t0,
  output [31:0] t1,
  output [31:0] t2,
  output [31:0] s0,
  output [31:0] s1,
  output [31:0] a0,
  output [3:0] MemWriteMask,
  output [31:0] MemWriteData
);

  wire branch_comp_1_p4, branch_comp_1_p5, control_logic_1_asel, control_logic_1_brun, control_logic_1_bsel,
       control_logic_1_memwen, control_logic_1_pcsel, control_logic_1_regwen, partial_load_1_p6;
  wire [1:0] control_logic_1_wbsel;
  wire [2:0] control_logic_1_immsel;
  wire [3:0] control_logic_1_alusel;
  wire [31:0] adder_1_out, imm_gen_1_immediate, multiplexer_1_out, multiplexer_2_out, multiplexer_3_out,
       multiplexer_4_out, multiplexer_5_out, partial_load_1_p7, regfile_1_readdata1, regfile_1_readdata2,
       register_1_q, register_2_q, register_3_q;

  Multiplexer #(.width(32)) multiplexer_1 (
    .in0(adder_1_out), .in1(MemAddress), .out(multiplexer_1_out), .sel(control_logic_1_pcsel));
  Adder #(.width(32)) adder_1 (.a(ProgramCounter), .b(32'h4), .out(adder_1_out));  // open: cin, cout
  Register #(.width(32)) PC (.D(multiplexer_1_out), .clk(clk), .Q(ProgramCounter));  // open: en, clr
  Multiplexer #(.width(32)) multiplexer_2 (
    .in0(Instruction), .in1(32'h13), .out(multiplexer_2_out), .sel(control_logic_1_pcsel));
  Register #(.width(32)) register_1 (.D(adder_1_out), .clk(clk), .Q(register_1_q));  // open: en, clr
  Register #(.width(32)) register_2 (.D(ProgramCounter), .clk(clk), .Q(register_2_q));  // open: en, clr
  Register #(.width(32)) register_3 (.D(multiplexer_2_out), .clk(clk), .Q(register_3_q));  // open: en, clr
  control_logic control_logic_1 (
    .Instruction(register_3_q), .BrEq(branch_comp_1_p4), .BrLt(branch_comp_1_p5),
    .PCSel(control_logic_1_pcsel), .RegWEn(control_logic_1_regwen), .ImmSel(control_logic_1_immsel),
    .BrUn(control_logic_1_brun), .ASel(control_logic_1_asel), .BSel(control_logic_1_bsel),
    .ALUSel(control_logic_1_alusel), .MemWEn(control_logic_1_memwen), .WBSel(control_logic_1_wbsel));
  regfile regfile_1 (
    .ReadIndex1(register_3_q[19:15]), .ReadIndex2(register_3_q[24:20]), .WriteIndex(register_3_q[11:7]),
    .WriteData(multiplexer_5_out), .RegWEn(control_logic_1_regwen), .clk(clk), .ra(ra), .sp(sp), .t0(t0),
    .t1(t1), .t2(t2), .s0(s0), .s1(s1), .a0(a0), .ReadData1(regfile_1_readdata1),
    .ReadData2(regfile_1_readdata2));
  imm_gen imm_gen_1 (.Instruction(register_3_q), .ImmSel(control_logic_1_immsel), .Immediate(imm_gen_1_immediate));
  Multiplexer #(.width(32)) multiplexer_3 (
    .in0(register_2_q), .in1(regfile_1_readdata1), .out(multiplexer_3_out), .sel(control_logic_1_asel));
  Multiplexer #(.width(32)) multiplexer_4 (
    .in0(imm_gen_1_immediate), .in1(regfile_1_readdata2), .out(multiplexer_4_out), .sel(control_logic_1_bsel));
  alu alu_1 (.A(multiplexer_3_out), .B(multiplexer_4_out), .ALUSel(control_logic_1_alusel), .ALUResult(MemAddress));
  // branch_comp branch_comp_1: pin names not known; wires that end beside it: regfile_1_readdata1, regfile_1_readdata2, control_logic_1_brun, branch_comp_1_p4, branch_comp_1_p5
  Multiplexer #(.select(2), .width(32)) multiplexer_5 (
    .in0(partial_load_1_p7), .in1(MemAddress), .in2(register_1_q), .out(multiplexer_5_out),
    .sel(control_logic_1_wbsel));  // open: in3
  partial_store partial_store_1 (
    .Instruction(register_3_q), .MemAddress(MemAddress), .MemWEn(control_logic_1_memwen),
    .MemWriteMask(MemWriteMask), .DataToMem(MemWriteData));  // open: DataFromReg
  // partial_load partial_load_1: pin names not known; wires that end beside it: MemReadData, MemAddress, control_logic_1_memwen, register_3_q, MemAddress, partial_load_1_p6, partial_load_1_p7

  // Notes on the sheet:
  //   To IMEM
  //   IMEM (do **NOT** move this)
  //   From IMEM
  //   Inputs/Outputs for testing. Do **NOT** move these.
  //   To DMEM
  //   DMEM (do **NOT** move this)
  //   From DMEM
endmodule
